# Fritzing sketch registrador de temperatura sincrono (saved by Fritzing 1.0.1rc)
breadboards: 1

parts:
  Componente1 = Arduino Uno (Rev3)
  DS1 = DS18B20 1-Wire Temperature Sensor Probe Cable
  Componente2 = Real Time Clock Module - DS1307 RTC Breakout Board
  R1 = Resistor [tolerance=±5% power=0.25 resistance=4.7k package=THT]
  R2 = Resistor [tolerance=±5% power=0.25 resistance=4.7k package=THT]
  R3 = Resistor [tolerance=±5% power=0.25 resistance=4.7k package=THT]
  microSD1 = MicroSD Card Module

nets:
  N1: Componente1.A4/SDA, Componente2.SDA, R3.Pin_1
  N2: Componente1.A5/SCL, Componente2.SCL, R2.Pin_0
  N3: Componente1.D11_PWM/MOSI, microSD1.MOSI
  N4: Componente1.D12/MISO, microSD1.MISO
  N5: Componente1.D13/SCK, microSD1.SCK
  N6: Componente1.D2, DS1.shield, R1.Pin_0
  N7: Componente1.D4, microSD1.CS
  5V: Componente1.5V, DS1.VDD, Componente2.5V, R1.Pin_1, R2.Pin_1, R3.Pin_0, microSD1.VCC
  GND: Componente1.GND, DS1.GND, Componente2.GND, microSD1.GND
